# Fritzing sketch HomeAssistWaage (saved by Fritzing 0.9.3b)

parts:
  Bauteil1 = HX711 Weighing Sensor Module
  MCU1 = Wemos Lolin32lite
  S1 = Load Sensor - 50kg [part_number=SEN-10245]
  S2 = Load Sensor - 50kg [part_number=SEN-10245]
  S3 = Load Sensor - 50kg [part_number=SEN-10245]
  S4 = Load Sensor - 50kg [part_number=SEN-10245]
  U1 = LIPO-1000mAh [package=lipo-1000]
  L1 = Inductor [package="0603 [SMD]"]  # not connected
  L2 = Inductor [package="0603 [SMD]"]
  TFT1 = Color 320x240 TFT Display, ILI9341 Controller Chip
  S5 = Pushbutton [package=THT]
  S6 = Pushbutton [package=THT]
  S7 = Pushbutton [package=THT]

nets:
  N1: Bauteil1.VCC, MCU1.pin_24
  N2: Bauteil1.GND, MCU1.pin_13, S7.leg0
  N3: Bauteil1.DO/RX, MCU1.pin_21
  N4: Bauteil1.CK/TX, MCU1.pin_22
  N5: Bauteil1.E+, S4.R
  N6: Bauteil1.E-, S1.R
  N7: Bauteil1.A+, S2.R
  N8: Bauteil1.A-, S3.R
  N9: MCU1.pin_5, TFT1.SDO_(MISO)
  N10: MCU1.pin_6, TFT1.LED
  N11: MCU1.pin_7, TFT1.SCK
  N12: MCU1.pin_8, TFT1.SDI_(MOSI)
  N13: MCU1.pin_9, TFT1.D/C
  N14: MCU1.pin_10, TFT1.Reset
  N15: MCU1.pin_11, TFT1.CS
  N16: MCU1.pin_14, U1.+
  N17: MCU1.pin_15, U1.-
  N18: MCU1.pin_16, L2.pin_0, S7.leg1
  N19: MCU1.pin_26, S6.leg1
  N20: MCU1.pin_27, S5.leg1
  N21: MCU1.pin_28, TFT1.VCC
  N22: S1.B, S4.B
  N23: S1.W, S3.W
  N24: S2.W, S4.W

custom parts:
  HX711 Weighing Sensor Module: HX711 is a precision 24-bit analog-to-digital converter (ADC) designed for weigh scales and industrial control applications to interface directly with a bridge sensor.
  Wemos Lolin32lite: Wemos Lolinlite32 wifi and blue tooth board based on the ESP-32 cpu, digital I/Os 19, analog inputs 6, clock 240mhz, Flash 4Mbytes, lipo battery charger (500ma connection broken out on breadboard but not pcb), usb.
  Load Sensor - 50kg: Half-wheatstone bridge Load Cell modified from the Fritzing Repo This load sensor, sometimes called a strain gauge, is the same one found in digital bathroom scales (you know, the ones you use in January for your New Year's resolutions, and then forget about a month later). This sensor can measure up to about 110 pounds.
  Color 320x240 TFT Display, ILI9341 Controller Chip: 2.2" TFT Display with ILI9341 Controller
